# Fritzing sketch arduinoclass1_breadboard (saved by Fritzing 0.9.2b)
breadboards: 1

parts:
  Part1 = Adafruit Pro Trinket 5V 16MHz [part_number="Adafruit #2000"]
  R1 = Resistor [tolerance=±5% resistance=220 package="1206 [SMD]"]
  LED1 = LEDs [package=led10mm]
  S1 = Pushbutton [package="[SMD]"]

nets:
  N1: Part1.GND, LED1.C, S1.Pin_1, S1.Pin_2
  N2: Part1.D4, R1.Pin_0
  N3: Part1.D3, S1.Pin_3, S1.Pin_4

custom parts:
  Adafruit Pro Trinket 5V 16MHz: Trinket's got a big sister in town - the Pro Trinket 5V! Pro Trinket combines everything you love about Trinket with the familiarity of the common core Arduino chip, the ATmega328. It's like an Arduino Pro Mini with more pins and USB tossed in, so delicious. Trinket's a year old now, and while its been great to see tons of tiny projects, sometimes you just need more pins, more FLASH, and more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
